# Fritzing sketch Arduino_as_ISP (saved by Fritzing 0.9.3b)
breadboards: 1

parts:
  Componente1 = Arduino Uno (Rev3)
  U1 = attiny85 [package=dip]

nets:
  N1: Componente1.D10_PWM/SS, U1.Pin_1
  N2: Componente1.D11_PWM/MOSI, U1.Pin_5
  N3: Componente1.D12/MISO, U1.Pin_6
  N4: Componente1.D13/SCK, U1.Pin_7
  N5: Componente1.5V, U1.Pin_8
  N6: Componente1.GND, U1.Pin_4
