# Fritzing sketch RxTx_2pin_UNO_ATTiny (saved by Fritzing 0.9.3b)
breadboards: 1

parts:
  Componente1 = Arduino Uno (Rev3)
  Componente2 = NRF24L01+ Breakout Board
  JP1 = Header 8 [package=1x08_smd]
  JP4 = Header 1 [package=1x01_offset]
  JP5 = Header 1 [package=1x01_offset]
  U1 = attiny85 [package=dip]
  LED1 = LED - 5mm [color="Green (555nm)" package="5 mm [THT]"]
  R1 = Resistor [tolerance=±5% resistance=220 package="0603 [SMD]"]
  JP2 = Header 8 [package=1x08_smd]
  R2 = Resistor [tolerance=±5% resistance=10k package=THT]
  R3 = Resistor [tolerance=±5% resistance=220 package=THT]
  C1 = Capacitor [package=cap-pth-small2]

nets:
  N1: Componente1.D5_PWM, JP4.1
  N2: Componente1.D6_PWM, JP5.1
  N3: Componente1.5V, U1.Pin_8
  N4: Componente1.GND, U1.Pin_4, R1.Pin_0, C1.1
  N5: Componente2.GND, JP1.8
  N6: Componente2.VCC, JP1.7
  N7: Componente2.CE, Componente2.CS, JP1.1, JP1.2, JP2.4, JP2.6, R3.Pin_1, C1.2
  N8: Componente2.SCK, JP1.3, U1.Pin_7, JP2.1, R3.Pin_0
  N9: Componente2.MOSI, JP1.4, U1.Pin_6, JP2.3, R2.Pin_1
  N10: Componente2.MISO, JP1.5, JP2.2, R2.Pin_0
  N11: U1.Pin_3, LED1.anode
  N12: LED1.cathode, R1.Pin_1

notes:
  YL - SCK | BL - MI | GR - MO | OR - CSN | PU - IRQ | RD - CE
  Receiver
  Transmitter
  YL - SCK | GR - MOMI
