# Fritzing sketch Rx_UNO (saved by Fritzing 0.9.3b)

parts:
  Componente1 = Arduino Uno (Rev3)
  Componente2 = NRF24L01+ Breakout Board
  JP1 = Header 8 [package=1x08_smd]
  JP2 = Header 8 [package=1x08_smd]

nets:
  N1: Componente1.D8, Componente2.CE, JP1.1, JP2.6
  N2: Componente1.D9_PWM, JP2.5
  N3: Componente1.D10_PWM/SS, Componente2.CS, JP1.2, JP2.4
  N4: Componente1.D11_PWM/MOSI, Componente2.MOSI, JP1.4, JP2.3
  N5: Componente1.D12/MISO, Componente2.MISO, JP1.5, JP2.2
  N6: Componente1.D13/SCK, Componente2.SCK, JP1.3, JP2.1
  N7: Componente2.GND, JP1.8
  N8: Componente2.VCC, JP1.7

notes:
  YL - SCK | BL - MI | GR - MO | OR - CSN | PU - IRQ | RD - CE
  Receiver
