# Fritzing sketch Tx_2pin_ATTiny85_button (saved by Fritzing 0.9.3b)
breadboards: 1

parts:
  Componente2 = NRF24L01+ Breakout Board
  JP1 = Header 8 [package=1x08_smd]
  U1 = attiny85 [package=dip]
  LED1 = LED - 5mm [color="Green (555nm)" package="5 mm [THT]"]
  R1 = Resistor [tolerance=±5% resistance=220 package="0603 [SMD]"]
  JP2 = Header 8 [package=1x08_smd]
  R2 = Resistor [tolerance=±5% resistance=10k package=THT]
  R3 = Resistor [tolerance=±5% resistance=220 package=THT]
  C1 = Capacitor [package=cap-pth-small2]
  R4 = Resistor [tolerance=±5% resistance=10 package=THT]
  VCC1 = Battery
  S2 = Round Pushbutton

nets:
  N1: Componente2.GND, JP1.8
  N2: Componente2.VCC, JP1.7
  N3: Componente2.CE, Componente2.CS, JP1.1, JP1.2, JP2.4, JP2.6, R3.Pin_1, C1.2
  N4: Componente2.SCK, JP1.3, U1.Pin_6, JP2.1, R3.Pin_0
  N5: Componente2.MOSI, JP1.4, U1.Pin_5, JP2.3, R2.Pin_1
  N6: Componente2.MISO, JP1.5, JP2.2, R2.Pin_0
  N7: U1.Pin_2, R4.Pin_0
  N8: U1.Pin_3, LED1.anode, S2.leg1
  N9: U1.Pin_4, R1.Pin_0, C1.1, R4.Pin_1, VCC1.-
  N10: U1.Pin_8, VCC1.+
  N11: LED1.cathode, R1.Pin_1

notes:
  YL - SCK | BL - MI | GR - MO | OR - CSN | PU - IRQ | RD - CE
  Transmitter
  YL - SCK | GR - MOMI
