# Fritzing sketch Tx_ATTiny (saved by Fritzing 0.9.3b)
breadboards: 1

parts:
  Componente2 = NRF24L01+ Breakout Board
  JP1 = Header 8 [package=1x08_smd]
  U1 = attiny85 [package=dip]
  LED1 = LED - 5mm [color="Green (555nm)" package="5 mm [THT]"]
  R1 = Resistor [tolerance=±5% resistance=220 package="0603 [SMD]"]
  JP2 = Header 8 [package=1x08_smd]
  VCC1 = Battery

nets:
  N1: Componente2.GND, JP1.8, U1.Pin_4, R1.Pin_0, VCC1.-
  N2: Componente2.VCC, JP1.7, U1.Pin_8, VCC1.+
  N3: Componente2.CE, Componente2.CS, JP1.1, JP1.2, U1.Pin_2, JP2.4, JP2.6
  N4: Componente2.SCK, JP1.3, U1.Pin_7, JP2.1
  N5: Componente2.MOSI, JP1.4, U1.Pin_6, JP2.3
  N6: Componente2.MISO, JP1.5, U1.Pin_5, JP2.2
  N7: U1.Pin_3, LED1.anode
  N8: LED1.cathode, R1.Pin_1

notes:
  YL - SCK | BL - MI | GR - MO | OR - CSN | PU - IRQ | RD - CE
  Transmiter
