# Fritzing sketch nrf24_RxTx (saved by Fritzing 0.9.3b)
breadboards: 1

parts:
  Componente1 = Arduino Uno (Rev3)
  Componente2 = NRF24L01+ Breakout Board
  JP1 = Header 8 [package=1x08_smd]
  JP4 = Header 1 [package=1x01_offset]
  JP5 = Header 1 [package=1x01_offset]
  U1 = attiny85 [package=dip]
  LED1 = LED - 5mm [color="Green (555nm)" package="5 mm [THT]"]
  R1 = Resistor [tolerance=±5% resistance=220 package="0603 [SMD]"]
  JP2 = Header 8 [package=1x08_smd]
  JP6 = Header 8 [package=1x08_smd]

nets:
  N1: Componente1.D8, JP6.6
  N2: Componente1.D10_PWM/SS, JP6.4
  N3: Componente1.D11_PWM/MOSI, JP6.3
  N4: Componente1.D12/MISO, JP6.2
  N5: Componente1.D13/SCK, JP6.1
  N6: Componente1.D5_PWM, Componente2.MISO, JP1.5, JP4.1, U1.Pin_5, JP2.2
  N7: Componente1.D6_PWM, Componente2.MOSI, JP1.4, JP5.1, U1.Pin_6, JP2.3
  N8: Componente1.5V, U1.Pin_8
  N9: Componente1.GND, U1.Pin_4, R1.Pin_0
  N10: Componente2.GND, JP1.8
  N11: Componente2.VCC, JP1.7
  N12: Componente2.CE, Componente2.CS, JP1.1, JP1.2, U1.Pin_2, JP2.4, JP2.6
  N13: Componente2.SCK, JP1.3, U1.Pin_7, JP2.1
  N14: U1.Pin_3, LED1.anode
  N15: LED1.cathode, R1.Pin_1

notes:
  YL - SCK | BL - MI | GR - MO | OR - CSN | PU - IRQ | RD - CE
  Receiver
  Transmiter
